// Logisim project armazenamento-de-dados-em-parelelo.circ as structural Verilog: 1 circuit, main circuit main
module main (
  input  CARGA,
  input  X,
  input  Y,
  input  Z,
  input  H,
  input  in_6,
  output out_7
);

  wire CLOCK_out, d_ff_1_q, d_ff_2_q, d_ff_3_q, nand_1_out, nand_2_out, nand_3_out, nand_4_out, nand_5_out,
       nand_6_out, nand_7_out, nand_8_out, not_1_out, not_2_out, not_3_out, not_4_out, not_5_out, not_6_out,
       not_7_out, not_8_out, not_9_out, not_10_out, not_11_out, not_12_out;

  Clock #(.highDuration(2)) CLOCK (.out(CLOCK_out));
  nand nand_1 (nand_1_out, X, CARGA);
  not not_1 (not_1_out, nand_1_out);
  not not_2 (not_2_out, X);
  nand nand_2 (nand_2_out, CARGA, not_2_out);
  D_Flip_Flop #(.Pre_Clr_Positions("LEGACY"), .enable("true"), .NewFFLayout("false")) d_ff_1 (
    .clk(CLOCK_out), .D(in_6), .Q(d_ff_1_q), .preset(not_1_out), .reset(not_3_out));  // open: Qn, en
  not not_3 (not_3_out, nand_2_out);
  nand nand_3 (nand_3_out, Y, CARGA);
  D_Flip_Flop #(.Pre_Clr_Positions("LEGACY"), .enable("true"), .NewFFLayout("false")) d_ff_2 (
    .clk(CLOCK_out), .D(d_ff_1_q), .Q(d_ff_2_q), .preset(not_4_out), .reset(not_6_out));  // open: Qn, en
  not not_4 (not_4_out, nand_3_out);
  not not_5 (not_5_out, Y);
  nand nand_4 (nand_4_out, CARGA, not_5_out);
  not not_6 (not_6_out, nand_4_out);
  nand nand_5 (nand_5_out, Z, CARGA);
  not not_7 (not_7_out, nand_5_out);
  not not_8 (not_8_out, Z);
  nand nand_6 (nand_6_out, CARGA, not_8_out);
  D_Flip_Flop #(.Pre_Clr_Positions("LEGACY"), .enable("true"), .NewFFLayout("false")) d_ff_3 (
    .clk(CLOCK_out), .D(d_ff_2_q), .Q(d_ff_3_q), .preset(not_7_out), .reset(not_9_out));  // open: Qn, en
  not not_9 (not_9_out, nand_6_out);
  nand nand_7 (nand_7_out, CARGA, H);
  not not_10 (not_10_out, nand_7_out);
  not not_11 (not_11_out, H);
  D_Flip_Flop #(.Pre_Clr_Positions("LEGACY"), .enable("true"), .NewFFLayout("false")) d_ff_4 (
    .clk(CLOCK_out), .D(d_ff_3_q), .Q(out_7), .preset(not_10_out), .reset(not_12_out));  // open: Qn, en
  nand nand_8 (nand_8_out, not_11_out, CARGA);
  not not_12 (not_12_out, nand_8_out);
endmodule
