// Logisim project armazenamento-parelelo-palalelo.circ as structural Verilog: 1 circuit, main circuit main
module main (
  input  in_1,
  input  in_2,
  input  in_3,
  input  in_4,
  output out_5,
  output out_6,
  output out_7,
  output out_8
);

  wire clock_1_out;

  Clock clock_1 (.out(clock_1_out));
  D_Flip_Flop #(.Pre_Clr_Positions("LEGACY")) d_ff_1 (
    .clk(clock_1_out), .D(in_1), .Q(out_5), .preset(1'b0), .reset(1'b0));  // open: Qn
  D_Flip_Flop #(.Pre_Clr_Positions("LEGACY")) d_ff_2 (
    .clk(clock_1_out), .D(in_2), .Q(out_6), .preset(1'b0), .reset(1'b0));  // open: Qn
  D_Flip_Flop #(.Pre_Clr_Positions("LEGACY")) d_ff_3 (
    .clk(clock_1_out), .D(in_3), .Q(out_7), .preset(1'b0), .reset(1'b0));  // open: Qn
  D_Flip_Flop #(.Pre_Clr_Positions("LEGACY")) d_ff_4 (
    .clk(clock_1_out), .D(in_4), .Q(out_8), .preset(1'b0), .reset(1'b0));  // open: Qn
endmodule
