// Logisim project comparador-4-bits.circ as structural Verilog: 1 circuit, main circuit main
module main (
  input  B3,
  input  B2,
  input  B1,
  input  B0,
  input  A3,
  input  A2,
  input  A1,
  input  A0,
  output A___B,
  output B___A,
  output B___A_2
);

  wire and_1_out, and_2_out, and_3_out, and_4_out, and_5_out, and_6_out, and_7_out, and_8_out, and_9_out,
       and_10_out, and_11_out, and_12_out, or_1_out, or_2_out, xnor_1_out, xnor_2_out, xnor_3_out, xnor_4_out;

  xnor xnor_1 (xnor_1_out, A3, B3);
  xnor xnor_2 (xnor_2_out, A2, B2);
  xnor xnor_3 (xnor_3_out, A1, B1);
  xnor xnor_4 (xnor_4_out, A0, B0);
  and and_1 (and_1_out, A2, ~B2);  // AND_Gate
  and and_2 (and_2_out, A3, ~B3);  // AND_Gate
  and and_3 (and_3_out, xnor_1_out, and_1_out);
  and and_4 (and_4_out, xnor_2_out, xnor_1_out);
  and and_5 (and_5_out, A1, ~B1);  // AND_Gate
  and and_6 (and_6_out, xnor_3_out, xnor_2_out);
  and and_7 (and_7_out, A0, ~B0);  // AND_Gate
  and and_8 (and_8_out, and_4_out, and_5_out);
  and and_9 (and_9_out, and_6_out, xnor_1_out);
  and and_10 (and_10_out, xnor_1_out, xnor_2_out);
  and and_11 (and_11_out, xnor_3_out, xnor_4_out);
  or or_1 (or_1_out, and_2_out, and_3_out);
  or or_2 (or_2_out, and_8_out, and_12_out);
  and and_12 (and_12_out, and_9_out, and_7_out);
  and and_13 (A___B, and_10_out, and_11_out);
  or or_3 (B___A_2, or_1_out, or_2_out);
  nor nor_1 (B___A, A___B, B___A_2);
endmodule
