// Logisim project conversor-binario-decimal.circ as structural Verilog
module conversor_binario_decimal (
  input  A,
  input  B,
  input  C,
  input  D,
  output a_2,
  output b_2,
  output c_2,
  output d_2,
  output e,
  output f,
  output g,
  output h
);

  wire and_1_out, and_2_out, and_3_out, and_4_out, and_5_out, and_6_out, and_7_out, and_8_out, and_9_out,
       and_10_out, and_11_out, and_12_out, and_13_out, and_14_out, and_15_out, and_16_out, and_17_out,
       and_18_out, and_19_out, and_20_out, and_21_out, and_22_out, and_23_out, and_24_out, and_25_out,
       and_26_out, and_27_out, and_28_out, and_29_out, and_30_out, and_31_out, and_32_out, and_33_out,
       and_34_out, and_35_out, and_36_out, and_37_out, and_38_out, and_39_out, and_40_out, and_41_out,
       and_42_out, and_43_out, and_44_out, and_45_out, and_46_out, and_47_out, and_48_out, not_1_out,
       not_2_out, not_3_out, not_4_out, or_2_out, or_3_out, or_4_out, or_6_out, or_7_out, or_8_out, or_9_out,
       or_10_out, or_11_out, or_12_out, or_13_out;

  not not_1 (not_1_out, A);
  not not_2 (not_2_out, B);
  not not_3 (not_3_out, C);
  not not_4 (not_4_out, D);
  and and_1 (and_1_out, A, C);
  and and_2 (and_2_out, A, B);
  and and_3 (and_3_out, not_1_out, not_2_out);
  and and_4 (and_4_out, not_1_out, not_2_out);
  and and_5 (and_5_out, not_1_out, B);
  and and_6 (and_6_out, A, not_2_out);
  and and_7 (and_7_out, not_1_out, not_2_out);
  and and_8 (and_8_out, not_1_out, not_3_out);
  and and_9 (and_9_out, and_8_out, not_4_out);
  and and_10 (and_10_out, not_2_out, not_3_out);
  and and_11 (and_11_out, not_1_out, C);
  and and_12 (and_12_out, and_11_out, D);
  and and_13 (and_13_out, not_2_out, not_3_out);
  and and_14 (and_14_out, not_1_out, D);
  and and_15 (and_15_out, not_1_out, B);
  and and_16 (and_16_out, not_2_out, not_3_out);
  and and_17 (and_17_out, not_1_out, not_2_out);
  and and_18 (and_18_out, not_1_out, C);
  and and_19 (and_19_out, not_1_out, B);
  and and_20 (and_20_out, not_3_out, D);
  and and_21 (and_21_out, not_2_out, not_3_out);
  and and_22 (and_22_out, and_21_out, not_4_out);
  and and_23 (and_23_out, not_1_out, and_24_out);
  and and_24 (and_24_out, C, not_4_out);
  and and_25 (and_25_out, not_1_out, not_3_out);
  and and_26 (and_26_out, and_25_out, not_4_out);
  and and_27 (and_27_out, not_1_out, B);
  and and_28 (and_28_out, and_27_out, not_3_out);
  and and_29 (and_29_out, not_1_out, B);
  and and_30 (and_30_out, and_29_out, not_4_out);
  and and_31 (and_31_out, A, not_2_out);
  and and_32 (and_32_out, and_31_out, not_3_out);
  and and_33 (and_33_out, not_1_out, not_2_out);
  and and_34 (and_34_out, and_33_out, C);
  and and_35 (and_35_out, not_1_out, B);
  and and_36 (and_36_out, and_35_out, not_3_out);
  and and_37 (and_37_out, not_1_out, B);
  and and_38 (and_38_out, and_37_out, not_4_out);
  and and_39 (and_39_out, A, not_2_out);
  and and_40 (and_40_out, and_39_out, not_3_out);
  or or_1 (h, and_1_out, and_2_out);
  and and_41 (and_41_out, and_3_out, not_4_out);
  and and_42 (and_42_out, and_4_out, C);
  and and_43 (and_43_out, and_5_out, D);
  and and_44 (and_44_out, and_6_out, not_3_out);
  or or_2 (or_2_out, and_7_out, and_9_out);
  or or_3 (or_3_out, and_10_out, and_12_out);
  or or_4 (or_4_out, and_13_out, and_14_out);
  or or_5 (c_2, or_4_out, and_15_out);
  and and_45 (and_45_out, and_16_out, not_4_out);
  or or_6 (or_6_out, and_45_out, and_46_out);
  and and_46 (and_46_out, and_17_out, C);
  and and_47 (and_47_out, and_18_out, not_4_out);
  or or_7 (or_7_out, and_47_out, and_48_out);
  and and_48 (and_48_out, and_19_out, and_20_out);
  or or_8 (or_8_out, and_26_out, and_28_out);
  or or_9 (or_9_out, and_30_out, and_32_out);
  or or_10 (or_10_out, and_34_out, and_36_out);
  or or_11 (or_11_out, and_38_out, and_40_out);
  or or_12 (or_12_out, and_41_out, and_42_out);
  or or_13 (or_13_out, and_43_out, and_44_out);
  or or_14 (b_2, or_2_out, or_3_out);
  or or_15 (d_2, or_6_out, or_7_out);
  or or_16 (e, and_22_out, and_23_out);
  or or_17 (f, or_8_out, or_9_out);
  or or_18 (g, or_10_out, or_11_out);
  or or_19 (a_2, or_12_out, or_13_out);
  _7_Segment_Display u_7_segment_display_1 (.g(g), .f(f), .a(a_2), .b(b_2), .e(e), .d(d_2), .c(c_2), .dp(h));

  // Notes on the sheet:
  //   A
  //   B
  //   C
  //   D
  //   E
  //   F
  //   G
  //   H
endmodule
