// Logisim project dividor-frequencia-flip-flop.circ as structural Verilog: 1 circuit, main circuit main
module main (
  input  in_1
);

  wire clock_1_out, j_k_ff_1_q, j_k_ff_2_q, j_k_ff_3_q, j_k_ff_4_q;

  Clock clock_1 (.out(clock_1_out));
  J_K_Flip_Flop #(.trigger("falling"), .enable("true"), .NewFFLayout("false")) j_k_ff_1 (
    .J(in_1), .clk(clock_1_out), .K(in_1), .Q(j_k_ff_1_q));  // open: Qn, preset, en, reset
  J_K_Flip_Flop #(.trigger("falling"), .enable("true"), .NewFFLayout("false")) j_k_ff_2 (
    .J(in_1), .clk(j_k_ff_1_q), .K(in_1), .Q(j_k_ff_2_q));  // open: Qn, preset, en, reset
  J_K_Flip_Flop #(.trigger("falling"), .enable("true"), .NewFFLayout("false")) j_k_ff_3 (
    .J(in_1), .clk(j_k_ff_2_q), .K(in_1), .Q(j_k_ff_3_q));  // open: Qn, preset, en, reset
  J_K_Flip_Flop #(.trigger("falling"), .enable("true"), .NewFFLayout("false")) j_k_ff_4 (
    .J(in_1), .clk(j_k_ff_3_q), .K(in_1), .Q(j_k_ff_4_q));  // open: Qn, preset, en, reset
  // Digital_Oscilloscope digital_oscilloscope_1: pin names not known; wires that end beside it: clock_1_out, j_k_ff_1_q, j_k_ff_2_q, j_k_ff_3_q, j_k_ff_4_q
endmodule
