// Logisim project somador-4-bits.circ as structural Verilog: 1 circuit, main circuit main
module main (
  input  B3,
  input  B2,
  input  B1,
  input  B0,
  input  A3,
  input  A2,
  input  A1,
  input  A0,
  output S4,
  output S3,
  output S2,
  output S1,
  output Cout,
  output Cout_2,
  output Cout_3,
  output Cout_4
);

  wire and_1_out, and_2_out, and_3_out, and_4_out, and_5_out, and_6_out, and_7_out, and_8_out, xor_1_out,
       xor_2_out, xor_3_out, xor_4_out;

  xor xor_1 (xor_1_out, A0, B0);
  xor xor_2 (xor_2_out, A1, B1);
  xor xor_3 (xor_3_out, A2, B2);
  xor xor_4 (xor_4_out, A3, B3);
  xor xor_5 (S1, xor_1_out, 1'b0);
  and and_1 (and_1_out, xor_1_out, 1'b0);
  and and_2 (and_2_out, B0, A0);
  xor xor_6 (S2, xor_2_out, Cout);
  and and_3 (and_3_out, xor_2_out, Cout);
  and and_4 (and_4_out, B1, A1);
  xor xor_7 (S3, xor_3_out, Cout_2);
  and and_5 (and_5_out, xor_3_out, Cout_2);
  and and_6 (and_6_out, B2, A2);
  xor xor_8 (S4, xor_4_out, Cout_3);
  and and_7 (and_7_out, xor_4_out, Cout_3);
  and and_8 (and_8_out, B3, A3);
  or or_1 (Cout, and_1_out, and_2_out);
  or or_2 (Cout_2, and_3_out, and_4_out);
  or or_3 (Cout_3, and_5_out, and_6_out);
  or or_4 (Cout_4, and_7_out, and_8_out);
endmodule
